# Fritzing sketch montaje_medidor_CO2_powerbank (saved by Fritzing 0.9.6b)

parts:
  active_buzzer1 = Active buzzer [package=THT]
  U3 = NodeMCU v3.0
  CO2-Sensor1 = SCD30 [part_number=SCD30 package=THT]
  Part3 = NeoPixel [part_number=WS2812B]
  Power_plug1 = Power plug
  S1 = Toggle Switch [package=THT]

nets:
  GND: active_buzzer1.GND, U3.GND, CO2-Sensor1.GND, Part3.GND, Power_plug1.GND
  N1: active_buzzer1.Vcc, U3.D8
  N2: U3.D1, CO2-Sensor1.TX/SCL
  N3: U3.D2, CO2-Sensor1.RX/SDA
  3V3: U3.3V3, CO2-Sensor1.VDD
  N4: U3.D6, Part3.IN
  VIN: U3.Vin, Part3.VDD, S1.L2
  N5: Power_plug1.VCC, S1.COM

notes:
  5V
  PowerBank

custom parts:
  Active buzzer: Active buzzer 12 mm, 3-5 V
  NodeMCU v3.0: NodeMCU v3 Lua WIFI Development Board
  SCD30: CO2 , humidity, and temperature sensor * Current consumption: 19 mA @ 1 meas. per 2 s. * Digital interface UART or I2C * Company: Sensirion - The Sensor Company Electrical specifications * average current: 19 mA * max. current: 75 mA * DC supply: 3.3 V - 5.5 V Operation conditions * temperature: 0 – 50°C * humidity: 0 – 95 %RH * sensor lifetime: 15 years CO2-sensor: * NDIR CO 2 sensor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
  NeoPixel: Single unit of a NeoPixel, based on the bright RGB LED WS2812B. These ultra-bright LEDs have a constant-current driver cooked right into the LED package! The pixels are chainable - so you only need 1 pin/wire to control as many LEDs as you like.
